// Logisim project compiler-cpu.circ as structural Verilog: 3 circuits, main circuit main
module main (
  input  [31:0] in_1
);

  wire alu_1_equal, Clk, clock_1_out, control_1_dispchar, control_1_dispnum, control_1_dmwe, control_1_halt,
       control_1_pcaddsrc, control_1_pcen, control_1_rfr1src, control_1_rfwe, InputKey_out;
  wire [1:0] control_1_aluysrc, control_1_pcsrc, control_1_rfdinsrc, control_1_rfrwsrc;
  wire [3:0] control_1_aluop, Disp_q_2, Disp_q_3, Disp_q_4, Disp_q_5, Disp_q_6;
  wire [4:0] insanalyse_1_rd, insanalyse_1_rs, insanalyse_1_rt, insanalyse_1_shamt, multiplexer_2_out,
       multiplexer_3_out;
  wire [5:0] insanalyse_1_funct, insanalyse_1_op;
  wire [11:0] Disp_q;
  wire [15:0] insanalyse_1_immediate16;
  wire [25:0] insanalyse_1_immediate26;
  wire [31:0] adder_1_out, adder_2_out, alu_1_result, bit_extender_1_out, bit_extender_2_out,
       bit_extender_3_out, bit_extender_4_out, main_1_a0_value, main_1_reg1, main_1_reg2_2, main_1_v0_value,
       multiplexer_1_out, multiplexer_4_out, multiplexer_5_out, multiplexer_6_out, PC_q, ram_1_data,
       rom_1_data;

  assign bit_extender_1_out = {{6{1'b0}}, insanalyse_1_immediate26};  // Bit_Extender bit_extender_1
  Multiplexer #(.select(2), .width(32), .enable("false")) multiplexer_1 (
    .in0(main_1_reg1), .in1(adder_1_out), .in2(adder_2_out), .in3(bit_extender_1_out),
    .out(multiplexer_1_out), .sel(control_1_pcsrc));
  Register #(.width(32)) PC (.D(multiplexer_1_out), .en(control_1_pcen), .Q(PC_q), .clk(Clk), .clr(1'b0));
  Adder #(.width(32)) adder_1 (.a(32'h1), .b(PC_q), .out(adder_1_out), .cin(1'b0));  // open: cout
  Hex_Digit_Display hex_digit_display_1 (.value(Disp_q_5), .dp(1'b0));
  Hex_Digit_Display hex_digit_display_2 (.value(Disp_q_6), .dp(1'b0));
  Hex_Digit_Display hex_digit_display_3 (.value(Disp_q_3), .dp(1'b0));
  Hex_Digit_Display hex_digit_display_4 (.value(Disp_q_4), .dp(1'b0));
  // Probe on {Disp_q_6, Disp_q_5, Disp_q_4, Disp_q_3, Disp_q_2, Disp_q}
  Hex_Digit_Display hex_digit_display_5 (.value(Disp_q[11:8]), .dp(1'b0));
  Hex_Digit_Display hex_digit_display_6 (.value(Disp_q_2), .dp(1'b0));
  Hex_Digit_Display hex_digit_display_7 (.value(Disp_q[7:4]), .dp(1'b0));
  Hex_Digit_Display hex_digit_display_8 (.value(Disp_q[3:0]), .dp(1'b0));
  ROM #(.addrWidth(10), .dataWidth(32)) rom_1 (.addr(PC_q[9:0]), .data(rom_1_data), .sel(1'b1));
  TTY tty_1 (.data(main_1_a0_value[6:0]), .clk(Clk), .we(control_1_dispchar));  // open: clr
  Clock clock_1 (.out(clock_1_out));
  and and_1 (Clk, clock_1_out, ~control_1_halt);  // AND_Gate
  Register #(.width(32), .trigger("high")) Disp (
    .D(main_1_a0_value), .en(1'b1), .Q({Disp_q_6, Disp_q_5, Disp_q_4, Disp_q_3, Disp_q_2, Disp_q}),
    .clk(control_1_dispnum), .clr(1'b0));
  InsAnalyse insanalyse_1 (
    .Ins(rom_1_data), .OP(insanalyse_1_op), .Rs(insanalyse_1_rs), .Rt(insanalyse_1_rt), .Rd(insanalyse_1_rd),
    .Shamt(insanalyse_1_shamt), .funct(insanalyse_1_funct), .Immediate16(insanalyse_1_immediate16),
    .Immediate26(insanalyse_1_immediate26));
  Button InputKey (.out(InputKey_out));
  Control control_1 (
    .Equal(alu_1_equal), .v0(main_1_v0_value), .OP(insanalyse_1_op), .funct(insanalyse_1_funct),
    .PCSrc(control_1_pcsrc), .PCAddSrc(control_1_pcaddsrc), .PCEn(control_1_pcen),
    .RFR1Src(control_1_rfr1src), .RFRWSrc(control_1_rfrwsrc), .RFDinSrc(control_1_rfdinsrc),
    .RFWE(control_1_rfwe), .ALUYSrc(control_1_aluysrc), .ALUOP(control_1_aluop), .DMWE(control_1_dmwe),
    .Halt(control_1_halt), .DispNum(control_1_dispnum), .Input(InputKey_out), .DispChar(control_1_dispchar));
  Multiplexer #(.width(5), .enable("false")) multiplexer_2 (
    .in0(insanalyse_1_rs), .in1(insanalyse_1_rt), .out(multiplexer_2_out), .sel(control_1_rfr1src));
  // Probe on in_1
  Multiplexer #(.select(2), .width(5), .enable("false")) multiplexer_3 (
    .in0(insanalyse_1_rt), .in1(insanalyse_1_rd), .in2({5{1'b1}}), .in3(5'b00010), .out(multiplexer_3_out),
    .sel(control_1_rfrwsrc));
  Multiplexer #(.select(2), .width(32), .enable("false")) multiplexer_4 (
    .in0(adder_2_out), .in1(ram_1_data), .in2(alu_1_result), .in3(in_1), .out(multiplexer_4_out),
    .sel(control_1_rfdinsrc));
  regfile_main main_1 (
    .Reg1_num(multiplexer_2_out), .Reg2(insanalyse_1_rt), .Write_Reg_num(multiplexer_3_out),
    .Din(multiplexer_4_out), .Write_Enable(control_1_rfwe), .Clock(Clk), .Reg1(main_1_reg1),
    .Reg2_2(main_1_reg2_2), .v0_Value(main_1_v0_value), .a0_Value(main_1_a0_value));  // open: s0_Value, s1_Value, s2_Value, ra_Value
  assign bit_extender_2_out = {{27{1'b0}}, insanalyse_1_shamt};  // Bit_Extender bit_extender_2
  assign bit_extender_3_out = {{16{insanalyse_1_immediate16[15]}}, insanalyse_1_immediate16};  // Bit_Extender bit_extender_3
  assign bit_extender_4_out = {{16{1'b0}}, insanalyse_1_immediate16};  // Bit_Extender bit_extender_4
  Multiplexer #(.select(2), .width(32), .enable("false")) multiplexer_5 (
    .in0(main_1_reg2_2), .in1(bit_extender_2_out), .in2(bit_extender_3_out), .in3(bit_extender_4_out),
    .out(multiplexer_5_out), .sel(control_1_aluysrc));
  ALU alu_1 (
    .AluOP(control_1_aluop), .X(main_1_reg1), .Equal(alu_1_equal), .Result(alu_1_result),
    .Y(multiplexer_5_out));  // open: Signed_Overflow, Result_2, UnSigned_Overflow
  Multiplexer #(.width(32), .enable("false")) multiplexer_6 (
    .in0({32{1'b0}}), .in1(bit_extender_3_out), .out(multiplexer_6_out), .sel(control_1_pcaddsrc));
  Adder #(.width(32)) adder_2 (.a(adder_1_out), .b(multiplexer_6_out), .out(adder_2_out), .cin(1'b0));  // open: cout
  RAM #(.addrWidth(10), .dataWidth(32), .bus("separate")) ram_1 (
    .addr(alu_1_result[9:0]), .din(main_1_reg2_2), .data(ram_1_data), .str(control_1_dmwe), .sel(1'b1),
    .clk(Clk), .ld(1'b1), .clr(1'b0));

  // Notes on the sheet:
  //   contents of rom_1 (hex, n*v repeats v):
  //   341d03ff 341e03ff c000cb7 3402000a c afbf0000 afbefffc 3a0f021 34010030 afa1ffd4 3a1e822 8fc8ffdc
  //   34080000 afc8ffdc 8fc9ffd8 34090001 afc9ffd8 8fcaffe0 1205021 afcaffe0 8fcbffe4 805821 afcbffe4
  //   114b0004 14b082a 2021ffff 10200001 8000c2d 8fccffe8 1006021 afccffe8 8fcdffec 1206821 afcdffec
  //   18d4020 afc8ffdc 8fcefff0 1207021 afcefff0 8fcffff4 340f0001 afcffff4 1cf4820 afc9ffd8 8000c11
  //   8fd0fff8 1008021 afd0fff8 8fa10004 3a1e820 8fbf0000 8fbefffc 2001021 3e00008 afbf0000 afbefffc
  //   3a0f021 34010030 afa1ffd4 3a1e822 8fc8ffdc 34080001 afc8ffdc 8fc9ffd8 34090001 afc9ffd8 8fcaffe0
  //   1205021 afcaffe0 8fcbffe4 805821 afcbffe4 114b0004 14b082a 2021ffff 10200001 8000c69 8fccffe8
  //   1006021 afccffe8 8fcdffec 1206821 afcdffec 23bdfff8 afa40004 afa50008 1802021 1a02821 42400 52c00
  //   c000e4d 404021 8fa40004 8fa50008 23bd0008 afc8ffdc 8fcefff0 1207021 afcefff0 8fcffff4 340f0001
  //   afcffff4 1cf4820 afc9ffd8 8000c42 8fd0fff8 1008021 afd0fff8 8fa10004 3a1e820 8fbf0000 8fbefffc
  //   2001021 3e00008 afbf0000 afbefffc 3a0f021 3401003c afa1ffc8 3a1e822 8fc8ffd0 34080001 afc8ffd0
  //   8fc9ffcc 34090001 afc9ffcc 8fcaffe8 1205021 afcaffe8 8fcbffec 805821 afcbffec 114b0004 14b082a
  //   2021ffff 10200001 8000cae 8fccffd8 1006021 afccffd8 8fcdffdc 1206821 afcdffdc 23bdfff8 afa40004
  //   afa50008 1802021 1a02821 42400 52c00 c000e4d 404021 8fa40004 8fa50008 23bd0008 afc8ffd0 8fceffd4
  //   8fcfffe0 1c07821 afcfffe0 8fd0ffe4 1008021 afd0ffe4 1f07020 afceffd4 8fd1fff0 1208821 afd1fff0
  //   8fd2fff4 34120001 afd2fff4 2324820 afc9ffcc 8000c7e 8fd3fff8 1c09821 afd3fff8 8fa10004 3a1e820
  //   8fbf0000 8fbefffc 2601021 3e00008 afbf0000 afbefffc 3a0f021 3401003c afa1ffc8 3a1e822 34040049
  //   3402000b c 3404006e 3402000b c 34040070 3402000b c 34040075 3402000b c 34040074 3402000b c 34040020
  //   3402000b c 3404006e 3402000b c 34040020 3402000b c 3404006e 3402000b c 3404006f 3402000b c 34040077
  //   3402000b c 3404000d 3402000b c 34020005 c 8fc8ffcc 404021 3404006e 3402000b c 34040020 3402000b c
  //   34040069 3402000b c 34040073 3402000b c 34040020 3402000b c 3404006f 3402000b c 3404006e 3402000b c
  //   34040020 3402000b c 34040064 3402000b c 34040069 3402000b c 34040067 3402000b c 34040069 3402000b c
  //   34040074 3402000b c 34040073 3402000b c 34040020 3402000b c 3404006e 3402000b c 3404006f 3402000b c
  //   34040077 3402000b c 3404000d 3402000b c 8fc9ffe0 1004821 afc9ffe0 1202021 afc8ffcc afc9ffe0 c000c72
  //   8fc8ffd0 404021 8fc9ffe4 1004821 afc9ffe4 1202021 34020001 c 34040054 3402000b c 34040068 3402000b c
  //   34040065 3402000b c 34040020 3402000b c 34040074 3402000b c 3404006f 3402000b c 34040074 3402000b c
  //   34040061 3402000b c 3404006c 3402000b c 34040020 3402000b c 34040066 3402000b c 34040061 3402000b c
  //   34040063 3402000b c 34040074 3402000b c 3404006f 3402000b c 34040072 3402000b c 34040069 3402000b c
  //   34040061 3402000b c 3404006c 3402000b c 34040020 3402000b c 34040069 3402000b c 34040073 3402000b c
  //   34040020 3402000b c 3404006f 3402000b c 3404006e 3402000b c 34040020 3402000b c 34040064 3402000b c
  //   34040069 3402000b c 34040067 3402000b c 34040069 3402000b c 34040074 3402000b c 34040073 3402000b c
  //   3404000d 3402000b c 8fcaffcc 8fcbffe8 1405821 afcbffe8 1602021 afc8ffd0 afc9ffe4 afcaffcc afcbffe8
  //   c000c05 8fc8ffd4 404021 8fc9ffec 1004821 afc9ffec 1202021 34020001 c 34040054 3402000b c 34040068
  //   3402000b c 34040065 3402000b c 34040020 3402000b c 34040073 3402000b c 34040075 3402000b c 3404006d
  //   3402000b c 34040020 3402000b c 34040069 3402000b c 34040073 3402000b c 34040020 3402000b c 3404006f
  //   3402000b c 3404006e 3402000b c 34040020 3402000b c 34040064 3402000b c 34040069 3402000b c 34040067
  //   3402000b c 34040069 3402000b c 34040074 3402000b c 34040073 3402000b c 3404000d 3402000b c 8fcaffcc
  //   8fcbfff0 1405821 afcbfff0 1602021 afc8ffd4 afc9ffec afcaffcc afcbfff0 c000c36 8fc8ffd8 404021
  //   8fc9fff4 1004821 afc9fff4 1202021 34020001 c 34040054 3402000b c 34040068 3402000b c 34040065
  //   3402000b c 34040020 3402000b c 34040066 3402000b c 34040061 3402000b c 34040063 3402000b c 34040074
  //   3402000b c 3404006f 3402000b c 34040072 3402000b c 34040069 3402000b c 34040061 3402000b c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
endmodule

module InsAnalyse (
  input  [31:0] Ins,
  output [5:0] OP,
  output [4:0] Rs,
  output [4:0] Rt,
  output [4:0] Rd,
  output [4:0] Shamt,
  output [5:0] funct,
  output [15:0] Immediate16,
  output [25:0] Immediate26
);


  assign funct = Ins[5:0];
  assign Immediate16 = Ins[15:0];
  assign Immediate26 = Ins[25:0];
  assign OP = Ins[31:26];
  assign Rd = Ins[15:11];
  assign Rs = Ins[25:21];
  assign Rt = Ins[20:16];
  assign Shamt = Ins[10:6];
endmodule

module Control (
  input  Equal,
  input  [31:0] v0,
  input  [5:0] OP,
  input  [5:0] funct,
  input  Input,
  output [1:0] PCSrc,
  output PCAddSrc,
  output PCEn,
  output RFR1Src,
  output [1:0] RFRWSrc,
  output [1:0] RFDinSrc,
  output RFWE,
  output [1:0] ALUYSrc,
  output [3:0] ALUOP,
  output DMWE,
  output Halt,
  output DispNum,
  output DispChar
);

  wire add, addi, addiu, addu, \and , and_1_out, and_2_out, and_3_out, and_6_out, and_7_out, and_8_out,
       and_9_out, andi, beq, bne, counter_1_q, decoder_1_out0, decoder_2_out0, decoder_2_out1,
       decoder_5_out0, decoder_5_out1, j, jal, jr, lw, \nor , not_1_out, not_2_out, \or , ori, sll, slt,
       slti, sltu, sra, srl, sub, syscall, v0_1, v0_5, v0_10, v0_11;

  Decoder #(.select(5), .disabled(0)) decoder_1 (
    .out0(decoder_1_out0), .out2(j), .out3(jal), .out4(beq), .out5(bne), .out8(addi), .out9(addiu),
    .out10(slti), .out12(andi), .out13(ori), .sel(OP[4:0]), .en(decoder_2_out0));  // open: out1, out6, out7, out11, out14, out15, out16, out17, out18, out19, out20, out21, out22, out23, out24, out25, out26, out27, out28, out29, out30, out31
  Decoder #(.enable("false")) decoder_2 (.out0(decoder_2_out0), .out1(decoder_2_out1), .sel(OP[5]));
  Decoder #(.select(5), .disabled(0)) decoder_3 (
    .out3(lw), .out11(DMWE), .sel(OP[4:0]), .en(decoder_2_out1));  // open: out0, out1, out2, out4, out5, out6, out7, out8, out9, out10, out12, out13, out14, out15, out16, out17, out18, out19, out20, out21, out22, out23, out24, out25, out26, out27, out28, out29, out30, out31
  or or_1 (PCAddSrc, beq, bne);
  or or_2 (RFR1Src, sll, sra, srl);
  nor nor_1 (RFDinSrc[1], lw, jal);
  or or_3 (RFDinSrc[0], lw, syscall);
  and and_1 (and_1_out, syscall, ~v0_5);  // AND_Gate
  and and_2 (and_2_out, syscall, v0_10);
  and and_3 (and_3_out, syscall, v0_5);
  and and_4 (DispNum, syscall, v0_1);
  and and_5 (DispChar, syscall, v0_11);
  Decoder #(.select(5), .enable("false")) decoder_4 (
    .out1(v0_1), .out5(v0_5), .out10(v0_10), .out11(v0_11), .sel(v0[4:0]));  // open: out0, out2, out3, out4, out6, out7, out8, out9, out12, out13, out14, out15, out16, out17, out18, out19, out20, out21, out22, out23, out24, out25, out26, out27, out28, out29, out30, out31
  not not_1 (not_1_out, Equal);
  and and_6 (and_6_out, beq, Equal);
  and and_7 (and_7_out, bne, not_2_out);
  not not_2 (not_2_out, Equal);
  or or_4 (RFRWSrc[1], jal, syscall);
  nor nor_2 (RFWE, DMWE, beq, bne, j, jr, and_1_out);
  or or_5 (ALUYSrc[1], addi, addiu, andi, ori, lw, DMWE, slti);
  or or_6 (ALUYSrc[0], andi, sll, sra, srl, ori);
  or or_7 (ALUOP[3], \or , ori, \nor , slt, slti, sltu);
  Counter #(.width(1), .max('h1)) counter_1 (
    .Q(counter_1_q), .clk(and_3_out), .clr(Input));  // open: load, D, count, carry
  and and_8 (and_8_out, beq, Equal);
  and and_9 (and_9_out, bne, not_1_out);
  nor nor_3 (PCSrc[0], and_6_out, and_7_out, jr);
  or or_8 (RFRWSrc[0], syscall, add, addu, \and , sll, sra, srl, sub, \or , \nor , slt, sltu);
  or or_9 (ALUOP[2], add, addi, addiu, addu, \and , andi, sub, lw, DMWE, beq, bne, sltu);
  or or_10 (ALUOP[1], \and , andi, srl, sub, \nor , beq, bne, slt, slti);
  or or_11 (ALUOP[0], add, addi, addiu, addu, \and , andi, sra, lw, DMWE, slt, slti);
  or or_12 (Halt, and_2_out, counter_1_q);
  or or_13 (PCSrc[1], and_8_out, and_9_out, j, jal);
  Decoder #(.disabled(0)) decoder_5 (.out0(decoder_5_out0), .out1(decoder_5_out1), .sel(funct[5]), .en(decoder_1_out0));
  Decoder #(.select(5), .disabled(0)) decoder_6 (
    .out0(sll), .out2(srl), .out3(sra), .out8(jr), .out12(syscall), .sel(funct[4:0]), .en(decoder_5_out0));  // open: out1, out4, out5, out6, out7, out9, out10, out11, out13, out14, out15, out16, out17, out18, out19, out20, out21, out22, out23, out24, out25, out26, out27, out28, out29, out30, out31
  Decoder #(.select(5), .disabled(0)) decoder_7 (
    .out0(add), .out1(addu), .out2(sub), .out4(\and ), .out5(\or ), .out7(\nor ), .out10(slt), .out11(sltu),
    .sel(funct[4:0]), .en(decoder_5_out1));  // open: out3, out6, out8, out9, out12, out13, out14, out15, out16, out17, out18, out19, out20, out21, out22, out23, out24, out25, out26, out27, out28, out29, out30, out31

  assign PCEn = 1'b1;

  // Other names for the same wires on the sheet: sw = DMWE
endmodule
